# Fritzing sketch LFR Circuit diagram (saved by Fritzing 0.9.3b)
circuit board: 8.46667cm x 5.64444cm
breadboards: 1

parts:
  Nano1 = Arduino Nano v2.3
  L298N1 = L298N DC motor driver
  BAT1 = Battery Holders [package=battery-aa]
  BAT2 = Battery Holders [package=battery-aa]
  BAT3 = Battery Holders [package=battery-aa]
  M3 = gear-motor
  Keyes1 = Keyes IR Infrared Sensor Switch Module
  Keyes2 = Keyes IR Infrared Sensor Switch Module
  M4 = gear-motor

nets:
  GND: Nano1.GND, L298N1.GND, BAT3.+, Keyes2.GND
  N1: Nano1.D2, Keyes1.out
  N2: Nano1.D3, L298N1.ENB
  N3: Nano1.D4, L298N1.IN4
  N4: Nano1.D5, L298N1.IN3
  N5: Nano1.D6, L298N1.IN2
  N6: Nano1.D7, L298N1.IN1
  N7: Nano1.D9, L298N1.ENA
  N8: Nano1.D10, Keyes2.out
  +5V: Nano1.+5V, Keyes1.VCC
  VIN: Nano1.VIN, L298N1.5V
  N9: L298N1.OUT1, M3.pin_2
  N10: L298N1.OUT2, M3.pin_1
  N11: L298N1.OUT3, M4.pin_2
  N12: L298N1.OUT4, M4.pin_1
  N13: L298N1.12V, BAT1.-
  N14: BAT1.+, BAT2.-
  N15: BAT2.+, BAT3.-

notes:
  11.1V
  Designed by Shoaib Athar
  Project: Line Following Robot
  Controller: Arduino Nano
  Motor Driver: L298N
  Supply: 3S 11.1 V Battery

custom parts:
  L298N DC motor driver: 2x DC motor driver with 78M05 positive voltage regulator (7..35 V) L298N: max 46 V, 2 A Set 5 V Enable jumper to enable 5 V regultor (needed for the L298N) and +5 V output at screw terminal or supply external +5 V at screw terminal Set ENA and/or ENB to +5 V to enable motor permanently or supply ENA and/or ENB with PWM signal IN1 and IN2 set rotation directory for motor A (OUT1/OUT2) IN2 and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
  Keyes IR Infrared Sensor Switch Module: An infrared obstacle detector
